# Fritzing sketch Lab6 (saved by Fritzing 0.9.10b)
breadboards: 1

parts:
  Teensy1 = Teensy 4.0
  R1 = Resistor [tolerance=±5% resistance=220 package="0402 [SMD]"]
  R2 = Resistor [tolerance=±5% resistance=220 package="0402 [SMD]"]
  R3 = Resistor [tolerance=±5% resistance=220 package="0402 [SMD]"]
  LED1 = RGB LED - (4 legs) [package="5 mm [THT]"]
  R16 = Trimmer Potentiometer [maximum_resistance=10kΩ knob_status=50% power=0.5W package=THT]

nets:
  N1: Teensy1.pin_1, Teensy1.pin_32, LED1.common_anode, R16.leg1
  N2: Teensy1.pin_21, R1.Pin_0
  N3: Teensy1.pin_22, R2.Pin_0
  N4: Teensy1.pin_25, R3.Pin_0
  N5: Teensy1.pin_27, R16.wiper
  N6: Teensy1.pin_31, R16.leg2
  N7: R1.Pin_1, LED1.blue_cathode
  N8: R2.Pin_1, LED1.green_cathode
  N9: R3.Pin_1, LED1.red_cathode

notes:
  CST8227 - Interfacing
  Lab 06 - User Controlled LED Color
  Use a potentiometer as user input to control the LED color.
  @author Mostapha Abdelaziz (abde0138)

custom parts:
  Teensy 4.0: The Teensy is a complete USB-based microcontoller development system, in a very small footprint, capable of implementing many types of projects. All programming is done via the USB port. No special programmer is needed, only a standard micro-USB cable and a PC or Macintosh with a USB port.
